# Fritzing sketch 16.ST Link 0NB Heorhii Nechyporenko updated (saved by Fritzing 0.9.4)
circuit board: 16.4972cm x 8.91017cm

parts:
  R3 = Resistor [tolerance=±5% resistance=4.7k package=THT]
  STM32F103C8T6_being_Programmed = STM32F103C8T6 blue mini board
  R1(220) = Resistor [tolerance=±5% resistance=220 package="2512 [SMD]"]
  R2 = Resistor [tolerance=±5% resistance=4.7k package=THT]
  STM32F103C8T6_STLINK = STM32F103C8T6 blue mini board
  J1 = male pin header, 4 pins [form="♂ (male)"]
  J2 = rounded female alternating pin header, 4 pins [form="♀ (female rounded)"]  # not connected

nets:
  N1: R3.Pin_0, R2.Pin_1, STM32F103C8T6_STLINK.A0
  GND: R3.Pin_1, STM32F103C8T6_being_Programmed.G, STM32F103C8T6_being_Programmed.GND, STM32F103C8T6_STLINK.G, STM32F103C8T6_STLINK.GND, J1.pin4
  N2: STM32F103C8T6_being_Programmed.RST, STM32F103C8T6_STLINK.B0
  N3: R1(220).Pin_0, STM32F103C8T6_STLINK.B12
  N4: R1(220).Pin_1, STM32F103C8T6_STLINK.B14, J1.pin2
  N5: R2.Pin_0, STM32F103C8T6_STLINK.3.3V
  N6: STM32F103C8T6_STLINK.B13, J1.pin3
  N7: STM32F103C8T6_STLINK.5V, J1.pin1

notes:
  220
  4k7
  b12
  b14
  b0
  NRST
  A0
  Ground
  3.3V
  SWD
  SWDIO
  SWDCLK
  GND
