# Fritzing sketch 16.ST Link 0NB Heorhii Nechyporenko (saved by Fritzing 0.9.4)
circuit board: 8.46667cm x 5.64444cm

parts:
  R3 = Resistor [tolerance=±5% resistance=4.7k package=THT]
  STM32F103C8T6_being_Programmed = STM32F103C8T6 blue mini board
  STM32F103C8T6_STLINK = STM32F103C8T6 blue mini board
  R1(220) = Resistor [tolerance=±5% resistance=220 package="2512 [SMD]"]
  R2 = Resistor [tolerance=±5% resistance=4.7k package=THT]

nets:
  N1: R3.Pin_0, STM32F103C8T6_STLINK.A0, R2.Pin_1
  N2: R3.Pin_1, STM32F103C8T6_being_Programmed.GND, STM32F103C8T6_STLINK.G
  3.3V: STM32F103C8T6_being_Programmed.3.3V, STM32F103C8T6_being_Programmed.3.3, STM32F103C8T6_STLINK.3.3V, R2.Pin_0
  N3: STM32F103C8T6_being_Programmed.RST, STM32F103C8T6_STLINK.B0
  N4: STM32F103C8T6_being_Programmed.DIO, STM32F103C8T6_STLINK.B14, R1(220).Pin_1
  N5: STM32F103C8T6_being_Programmed.CLK, STM32F103C8T6_STLINK.B13
  N6: STM32F103C8T6_STLINK.B12, R1(220).Pin_0

notes:
  220
  4k7
